# Fritzing sketch MIDI Drums (saved by Fritzing 0.9.2b)
circuit board: 9.97186cm x 7.60118cm
breadboards: 1

parts:
  Nano = Arduino Nano (Rev3.0)
  switch1 = Rotary_Switch_12x1
  U1 = POT [package=pot_mammoth]
  VCC1 = 4 x AAA Battery Mount
  J1 = Piezo Speaker
  R1 = Resistor [tolerance=±5% resistance=1M package=THT]
  J2 = Piezo Speaker
  R2 = Resistor [tolerance=±5% resistance=1M package=THT]
  J3 = Piezo Speaker
  R3 = Resistor [tolerance=±5% resistance=1M package=THT]
  J4 = Piezo Speaker
  R4 = Resistor [tolerance=±5% resistance=1M package=THT]

nets:
  N1: Nano.GND, switch1.0, U1.S, VCC1.-, J1.pin1, R1.Pin_0, J2.pin1, R2.Pin_0, J3.pin1, R3.Pin_0, J4.pin1, R4.Pin_0
  N2: Nano.D2, switch1.1
  N3: Nano.D3, switch1.2
  N4: Nano.D4, switch1.3
  N5: Nano.D5, switch1.4
  N6: Nano.D6, switch1.5
  N7: Nano.A4, U1.A, J4.pin2, R4.Pin_1
  N8: Nano.A2, J3.pin2, R3.Pin_1
  N9: Nano.A1, J2.pin2, R2.Pin_1
  N10: Nano.A0, J1.pin2, R1.Pin_1
  N11: U1.E, VCC1.+
